# Fritzing sketch Circut Diagram ChemE Car EE Team 2017-2018 (saved by Fritzing 0.9.3b)

parts:
  Part1 = Arduino Prototyping Shield
  J1 = female pin header, 8 pins [form="♀ (female)"]
  J2 = female alternating pin header, 10 pins [form="♀ (female)"]
  J3 = female pin header, 6 pins [form="♀ (female)"]
  J4 = female pin header, 8 pins [form="♀ (female)"]
  J5 = female pin header, 1 pin [form="♀ (female)"]
  R1 = Resistor [tolerance=±5% resistance=100k package="0603 [SMD]"]
  C1 = Ceramic Capacitor [capacitance=1µF package="200 mil [THT, multilayer]"]
  R2 = Resistor [tolerance=±5% resistance=100k package="0603 [SMD]"]
  R3 = Resistor [tolerance=±5% resistance=100k package="0603 [SMD]"]
  R4 = Resistor [tolerance=±5% resistance=100k package="0603 [SMD]"]
  R5 = Resistor [tolerance=±5% resistance=100k package="0603 [SMD]"]
  Q1 = pnp-Powertransistor [package="TO220 [THT]"]

nets:
  N1: Part1.A0, Part1.N$76, Part1.N$118, J3.pin1, J5.pin1, R1.Pin_0, C1.0
  N2: Part1.A1, J3.pin2
  N3: Part1.A2, J3.pin3
  N4: Part1.A3, J3.pin4
  N5: Part1.A4, J3.pin5
  N6: Part1.A5, J3.pin6
  N7: Part1.D0(RX), J1.pin8
  N8: Part1.D1(TX), J1.pin7
  N9: Part1.D2, J1.pin6, R2.Pin_0
  N10: Part1.D3, J1.pin5, R3.Pin_0
  N11: Part1.D4, J1.pin4, R4.Pin_0
  N12: Part1.D5, J1.pin3, R5.Pin_0
  N13: Part1.D6, J1.pin2
  N14: Part1.D7, J1.pin1
  N15: Part1.IOREF, J4.pin1, J4.pin2
  N16: Part1.RESET, J4.pin3
  N17: Part1.3.3V, J4.pin4
  N18: Part1.+5V, J4.pin5
  N19: Part1.GND, Part1.N$85, Part1.N$86, Part1.N$406, Part1.N$407, Part1.N$409, Part1.N$412, J2.pin4, J4.pin6, J4.pin7, R1.Pin_1, C1.1, R2.Pin_1, R3.Pin_1, R4.Pin_1, R5.Pin_1
  N20: Part1.+9V, J4.pin8
  N21: Part1.D8, J2.pin10
  N22: Part1.D9, J2.pin9
  N23: Part1.D10, J2.pin8
  N24: Part1.D11, J2.pin7
  N25: Part1.D12, J2.pin6
  N26: Part1.D13, J2.pin5
  N27: Part1.AREF, J2.pin3
  N28: Part1.SDA, J2.pin2
  N29: Part1.SCL, J2.pin1
  N30: Part1.N$67, Q1.collector
  N31: Part1.N$87, Q1.base
  N32: Part1.N$178, Q1.emitter

notes:
  left to right: 1) Dig Light Sensor, 2) Button, 3) Smart Control Switch, 4) Other Switch
